# Fritzing sketch sketch-dht11 (saved by Fritzing 0.9.2b)
breadboards: 1

parts:
  DHT1 = DHT11 Humitidy and Temperature Sensor
  R1 = Resistor [tolerance=±5% resistance=4.7k package="0402 [SMD]"]
  U2 = ESP8266 WiFi Module [part_number=ESP8266]
  U3 = Breadboard Power Supply [package=THT]  # not connected

nets:
  VDD: DHT1.VDD, R1.Pin_0, U2.VCC, U2.CH_PD
  N1: DHT1.DATA, R1.Pin_1, U2.GPIO_2
  GND: DHT1.GND, U2.GND

custom parts:
  DHT11 Humitidy and Temperature Sensor: DHT11 Humidity and Temperature Sensor
  ESP8266 WiFi Module: Generic WiFi Module based on the ESP8266 with onboard PCB antenna and UART communications
  Breadboard Power Supply: Représentation Carte Breadboard Power Supply
