# Fritzing sketch sketch (saved by Fritzing 0.9.2b)
breadboards: 1

parts:
  DHT1 = DHT11 Humitidy and Temperature Sensor
  U1 = NodeMCU V3.0
  R1 = Resistor [tolerance=±5% resistance=4.7k package="0402 [SMD]"]
  DS1 = DS18B20 1-Wire Temperature Sensor [part_number=DS18B20]
  R2 = Resistor [tolerance=±5% resistance=4.7k package="0402 [SMD]"]

nets:
  VDD: DHT1.VDD, U1.3V3, R1.Pin_0, DS1.VDD, R2.Pin_0
  N1: DHT1.DATA, U1.D7, R1.Pin_1
  GND: DHT1.GND, U1.GND, DS1.GND
  N2: U1.D0, U1.RST
  N3: U1.D6, DS1.DQ, R2.Pin_1

custom parts:
  DHT11 Humitidy and Temperature Sensor: DHT11 Humidity and Temperature Sensor
  NodeMCU V3.0: ESP8266 based NodeMCU
